# Fritzing sketch Schaltplan (saved by Fritzing 0.9.3b)

parts:
  S1_HOCH = Pushbutton [package=THT]
  S6_VORWAERTS = Pushbutton [package=THT]
  S5_ZURUECK = Pushbutton [package=THT]
  S4_RECHTS = Pushbutton [package=THT]
  S2_RUNTER = Pushbutton [package=THT]
  S3_LINKS = Pushbutton [package=THT]
  4_Channel_Relay1 = 4 Channel Power Relay
  4_Channel_Relay2 = 4 Channel Power Relay
  Raspberry_Pi_1 = Raspberry Pi 3 [part_number=RPI-3-V1.2]
  U1 = LM2596 step down module
  L1 = Solenoid
  L2 = Solenoid
  L3 = Solenoid
  L4 = Solenoid
  L5 = Solenoid
  M1 = DC Motor
  L6 = Solenoid [part_number=Wasser]

nets:
  GND: S1_HOCH.leg0, S6_VORWAERTS.leg0, S5_ZURUECK.leg0, S4_RECHTS.leg0, S2_RUNTER.leg0, S3_LINKS.leg0, 4_Channel_Relay1.GND, 4_Channel_Relay2.GND, Raspberry_Pi_1.GND
  N1: S1_HOCH.leg1, Raspberry_Pi_1.GIPO26
  N2: S6_VORWAERTS.leg1, Raspberry_Pi_1.GPIO2
  N3: S5_ZURUECK.leg1, Raspberry_Pi_1.GIPO21
  N4: S4_RECHTS.leg1, Raspberry_Pi_1.GIPO4
  N5: S2_RUNTER.leg1, Raspberry_Pi_1.GIPO19
  N6: S3_LINKS.leg1, Raspberry_Pi_1.GPIO3
  N7: 4_Channel_Relay1.IN1, Raspberry_Pi_1.GIPO15
  N8: 4_Channel_Relay1.IN2, Raspberry_Pi_1.GIPO18
  N9: 4_Channel_Relay1.IN4, Raspberry_Pi_1.GIPO23
  VCC: 4_Channel_Relay1.VCC, 4_Channel_Relay2.VCC, Raspberry_Pi_1.5V
  12V: 4_Channel_Relay1.COM, 4_Channel_Relay2.COM, U1.IN+
  N10: 4_Channel_Relay1.NO#18, L4.pin2
  N11: 4_Channel_Relay1.NO#21, L5.pin2
  N12: 4_Channel_Relay1.NO#27, M1.pin_2
  N13: 4_Channel_Relay2.IN1, Raspberry_Pi_1.GIPO24
  N14: 4_Channel_Relay2.IN2, Raspberry_Pi_1.ID_SD
  N15: 4_Channel_Relay2.IN3, Raspberry_Pi_1.GIPO7
  N16: 4_Channel_Relay2.IN4, Raspberry_Pi_1.GIPO8
  N17: 4_Channel_Relay2.NO#18, L3.pin2
  N18: 4_Channel_Relay2.NO#21, L2.pin2
  N19: 4_Channel_Relay2.NO#24, L1.pin2
  N20: 4_Channel_Relay2.NO#27, L6.pin2
  GND_2: U1.IN-, U1.OUT-, L1.pin1, L2.pin1, L3.pin1, L4.pin1, L5.pin1, M1.pin_1, L6.pin1

notes:
  Ausgänge am
  Micro-USB-Stecker
  vom Raspberry Pi
  angeschlossen
  Paamestia, Anschlussplan, 2.0

custom parts:
  4 Channel Power Relay: A 4 channel power relay. The module operates at 5V.
  LM2596 step down module: LM2596 DC-DC step down power supply module 3 A.
